# Fritzing sketch pc_EL_fader (saved by Fritzing 0.9.3b)
circuit board: 3.49391cm x 2.80528cm
breadboards: 1

parts:
  U4 = OP27 - Low Noise, Precision Op Amp [part_number=TLC271]
  R4 = Resistor [tolerance=±10% resistance=1M package=THT]
  C2 = Capacitor [package=cap-pth-5mm]
  R5 = Resistor [tolerance=±5% resistance=82k package=THT]
  JP3 = Header 2 [part_number=EL package=jst-2-pth-kit]
  R6 = Resistor [tolerance=±5% resistance=38k package=THT]
  U5 = Voltage Regulator [part_number=LM317 package=to220-adj]
  JP4 = Header 2 [part_number=Vdd/GND package=jst-2-pth-kit]
  JP5 = Header 2 [part_number="PWM breakout" package=jst-2-pth-kit]
  U6 = female pin header, 3 pins [form="♀ (female)" part_number="EL driver"]

nets:
  N1: U4.-IN, R5.Pin_0, R6.Pin_1
  N2: U4.+IN, R4.Pin_1, C2.1
  GND: U4.-V, C2.2, JP3.2, R6.Pin_0, JP4.2, JP5.1, U6.pin2
  N3: U4.OUT, R5.Pin_1, U5.ADJ
  N4: U4.V+, U5.IN, JP4.1
  N5: R4.Pin_0, JP5.2
  N6: JP3.1, U6.pin1
  N7: U5.OUT, U6.pin3

notes:
  EL fader v0.1
