# Fritzing sketch pc_l298_breakout (saved by Fritzing 0.9.3b)
circuit board: 5.32694cm x 3.02683cm
breadboards: 1

parts:
  D1 = Rectifier Diode [part_number=1N4001 package="300 mil [THT]"]
  D2 = Rectifier Diode [part_number=1N4001 package="300 mil [THT]"]
  D3 = Rectifier Diode [part_number=1N4001 package="300 mil [THT]"]
  D4 = Rectifier Diode [part_number=1N4001 package="300 mil [THT]"]
  D7 = Rectifier Diode [part_number=1N4001 package="300 mil [THT]"]
  D6 = Rectifier Diode [part_number=1N4001 package="300 mil [THT]"]
  D8 = Rectifier Diode [part_number=1N4001 package="300 mil [THT]"]
  D5 = Rectifier Diode [part_number=1N4001 package="300 mil [THT]"]
  U1 = L298 [package=multiwatt15]
  R2 = Resistor [tolerance=±5% resistance=0.47 power=1W package=THT]
  R1 = Resistor [tolerance=±5% resistance=0.47 power=1W package=THT]
  JP1 = Header 2 [part_number=12V/GND package=jst-2-pth]
  JP2 = Header 2 [part_number=5V/GND package=jst-2-pth]
  JP3 = Header 3 [part_number=MotorIn1 package=jst-3-pth]
  JP4 = Header 3 [part_number=MotorIn2 package=jst-3-pth]
  JP5 = Header 2 [part_number=Motor1Out package=jst-2-pth]
  JP6 = Header 2 [part_number=MotorOut2 package=jst-2-pth]
  C1 = Ceramic Capacitor [capacitance=100nF package="200 mil [THT, multilayer]"]
  C2 = Ceramic Capacitor [capacitance=100nF package="200 mil [THT, multilayer]"]

nets:
  N1: D1.cathode, D2.cathode, D3.cathode, D4.cathode, U1.VS, JP1.1, C2.1
  N2: D1.anode, D5.cathode, U1.OUT1, JP5.1
  N3: D2.anode, D6.cathode, U1.OUT2, JP5.2
  N4: D3.anode, D7.cathode, U1.OUT3, JP6.1
  N5: D4.anode, D8.cathode, U1.OUT4, JP6.2
  GND: D7.anode, D6.anode, D8.anode, D5.anode, U1.GND, R2.Pin_0, R1.Pin_0, JP1.2, JP2.2, C1.0, C2.0
  N6: U1.CSA, R1.Pin_1
  N7: U1.IN1, JP3.2
  N8: U1.ENA, JP3.1
  N9: U1.IN2, JP3.3
  N10: U1.VLS, JP2.1, C1.1
  N11: U1.IN3, JP4.2
  N12: U1.ENB, JP4.1
  N13: U1.IN4, JP4.3
  N14: U1.CSB, R2.Pin_1

notes:
  pc_motor_controller v0.1
