# Fritzing sketch pc_module_shield_02 (saved by Fritzing 0.9.3b)
circuit board: 6.88566cm x 5.36311cm
breadboards: 1

parts:
  U1 = OP27 - Low Noise, Precision Op Amp [part_number=TLC271]
  Part1 = Arduino Uno (Rev3)
  R1 = Resistor [tolerance=±10% resistance=1M package=THT]
  R2 = Resistor [tolerance=±5% resistance=82k package=THT]
  R3 = Resistor [tolerance=±5% resistance=38k package=THT]
  U2 = Voltage Regulator [part_number=LM317 package=to220-adj]
  JP1 = Header 2 [part_number=Vdd/GND package=jst-2-pth-kit]
  JP2 = Header 2 [part_number=EL package=jst-2-pth-kit]
  JP3 = Header 3 [part_number=PulseSensor package=jst-3-pth]
  JP4 = Header 2 [part_number=ReedSwitch package=jst-2-pth-kit]
  R4 = Resistor [tolerance=±5% resistance=10k package=THT]
  C1 = Capacitor [package=cap-pth-5mm]
  JP5 = Header 3 [part_number=Motor1 package=jst-3-pth]
  JP7 = Header 2 [part_number=Vmotorlogic package=jst-2-pth-kit]
  U3 = female pin header, 1 pin [form="♀ (female)"]
  J2 = female pin header, 1 pin [form="♀ (female)"]
  J3 = female pin header, 1 pin [form="♀ (female)"]
  JP8 = Header 2 [part_number=Vservologic package=jst-2-pth-kit]
  JP9 = Header 2 [part_number=Servo package=jst-2-pth-kit]

nets:
  N1: U1.-IN, R2.Pin_0, R3.Pin_1
  N2: U1.+IN, R1.Pin_1, C1.1
  GND: U1.-V, Part1.GND, R3.Pin_0, JP1.2, JP2.2, JP3.3, R4.Pin_1, C1.2, JP7.2, J2.pin1, JP8.2
  N3: U1.OUT, R2.Pin_1, U2.ADJ
  N4: U1.V+, Part1.VIN, U2.IN, JP1.1
  N5: Part1.A0, JP3.1
  N6: Part1.A4/SDA, JP9.1
  N7: Part1.A5/SCL, JP9.2
  N8: Part1.D8, JP4.2, R4.Pin_0
  N9: Part1.D9_PWM, R1.Pin_0
  N10: Part1.D2, JP5.2
  N11: Part1.D3_PWM, JP5.3
  N12: Part1.D5_PWM, JP5.1
  N13: Part1.5V, JP3.2, JP4.1, JP7.1, JP8.1
  N14: U2.OUT, J3.pin1
  N15: JP2.1, U3.pin1

notes:
  pc_module_shield v0.4
