# Fritzing sketch pc_peltier (saved by Fritzing 0.9.3b)
circuit board: 6.72253cm x 1.63124cm
breadboards: 1

parts:
  Q1 = Basic FET N-Channel [part_number=IRF540NPBF package="TO220 [THT]"]
  J1 = female pin header, 3 pins [form="♀ (female)"]
  J2 = female pin header, 2 pins [form="♀ (female)"]
  Q2 = Basic FET N-Channel [part_number=IRF540NPBF package="TO220 [THT]"]
  J3 = female pin header, 3 pins [form="♀ (female)"]
  J4 = female pin header, 2 pins [form="♀ (female)"]
  Q3 = Basic FET N-Channel [part_number=IRF540NPBF package="TO220 [THT]"]
  J5 = female pin header, 3 pins [form="♀ (female)"]
  J6 = female pin header, 2 pins [form="♀ (female)"]
  Q4 = Basic FET N-Channel [part_number=IRF540NPBF package="TO220 [THT]"]
  J7 = female pin header, 3 pins [form="♀ (female)"]
  J8 = female pin header, 2 pins [form="♀ (female)"]
  Q5 = Basic FET N-Channel [part_number=IRF540NPBF package="TO220 [THT]"]
  J9 = female pin header, 3 pins [form="♀ (female)"]
  J10 = female pin header, 2 pins [form="♀ (female)"]
  Q6 = Basic FET N-Channel [part_number=IRF540NPBF package="TO220 [THT]"]
  J11 = female pin header, 3 pins [form="♀ (female)"]
  J12 = female pin header, 2 pins [form="♀ (female)"]

nets:
  N1: Q1.gate, J1.pin1
  N2: Q1.drain, J2.pin2
  N3: Q1.source, J1.pin3
  N4: J1.pin2, J2.pin1
  N5: Q2.gate, J3.pin1
  N6: Q2.drain, J4.pin2
  N7: Q2.source, J3.pin3
  N8: J3.pin2, J4.pin1
  N9: Q3.gate, J5.pin1
  N10: Q3.drain, J6.pin2
  N11: Q3.source, J5.pin3
  N12: J5.pin2, J6.pin1
  N13: Q4.gate, J7.pin1
  N14: Q4.drain, J8.pin2
  N15: Q4.source, J7.pin3
  N16: J7.pin2, J8.pin1
  N17: Q5.gate, J9.pin1
  N18: Q5.drain, J10.pin2
  N19: Q5.source, J9.pin3
  N20: J9.pin2, J10.pin1
  N21: Q6.gate, J11.pin1
  N22: Q6.drain, J12.pin2
  N23: Q6.source, J11.pin3
  N24: J11.pin2, J12.pin1
